// Digital circuit main.dig as structural Verilog
module main (
  input  rst,
  input  clk
);

  wire and_1_out, cmp_1_out, controller_1_pc_in_sel, controller_1_pc_load, controller_1_r1_pc_sel,
       controller_1_r2_imm_sel, controller_1_rf_write;
  wire [1:0] controller_1_rf_in_sel;
  wire [2:0] controller_1_lu_op;
  wire [3:0] controller_1_au_op, controller_1_memory_op;
  wire [4:0] decode_1_rd, decode_1_rs1, decode_1_rs2;
  wire [6:0] decode_1_opcode;
  wire [9:0] decode_1_funct;
  wire [31:0] add_1_s, alu_1_out, code_1_inst, decode_1_imm, memory_1_dout, multiplexer_1_out,
       multiplexer_2_out, multiplexer_3_out, multiplexer_4_out, pc_1_dout, pc_4_1_pc_out, regfile_1_r1,
       regfile_1_r2;

  Multiplexer #(.Bits(32)) multiplexer_1 (
    .sel(and_1_out), .in_0(pc_4_1_pc_out), .in_1(alu_1_out), .out(multiplexer_1_out));
  and and_1 (and_1_out, cmp_1_out, controller_1_pc_in_sel);
  pc_4 pc_4_1 (.pc_out(pc_4_1_pc_out), .pc(pc_1_dout));
  pc pc_1 (.clk(clk), .rst(rst), .load(controller_1_pc_load), .din(multiplexer_1_out), .dout(pc_1_dout));
  code code_1 (.pc(pc_1_dout), .inst(code_1_inst));
  // Probe on code_1_inst
  decode decode_1 (
    .inst(code_1_inst), .opcode(decode_1_opcode), .funct(decode_1_funct), .rs1(decode_1_rs1),
    .rs2(decode_1_rs2), .rd(decode_1_rd), .imm(decode_1_imm));
  regfile regfile_1 (
    .clk(clk), .rst(rst), .rs1(decode_1_rs1), .rs2(decode_1_rs2), .rd(decode_1_rd),
    .write(controller_1_rf_write), .din(multiplexer_4_out), .r1(regfile_1_r1), .r2(regfile_1_r2));
  controller controller_1 (
    .memory_op(controller_1_memory_op), .au_op(controller_1_au_op), .lu_op(controller_1_lu_op),
    .r1_pc_sel(controller_1_r1_pc_sel), .r2_imm_sel(controller_1_r2_imm_sel), .pc_load(controller_1_pc_load),
    .pc_in_sel(controller_1_pc_in_sel), .rf_write(controller_1_rf_write), .rf_in_sel(controller_1_rf_in_sel),
    .clk(clk), .rst(rst), .opcode(decode_1_opcode), .funct(decode_1_funct));
  Multiplexer #(.Bits(32)) multiplexer_2 (
    .sel(controller_1_r1_pc_sel), .in_0(regfile_1_r1), .in_1(pc_1_dout), .out(multiplexer_2_out));
  Multiplexer #(.Bits(32)) multiplexer_3 (
    .sel(controller_1_r2_imm_sel), .in_0(regfile_1_r2), .in_1(decode_1_imm), .out(multiplexer_3_out));
  cmp cmp_1 (.op(controller_1_lu_op), .in1(regfile_1_r1), .in2(regfile_1_r2), .out(cmp_1_out));
  alu alu_1 (.op(controller_1_au_op), .in1(multiplexer_2_out), .in2(multiplexer_3_out), .out(alu_1_out));
  // Probe on multiplexer_3_out
  Multiplexer #(.Selector_Bits(2), .Bits(32)) multiplexer_4 (
    .sel(controller_1_rf_in_sel), .in_0(alu_1_out), .in_1(memory_1_dout), .in_2(add_1_s), .in_3({32{1'b0}}),
    .out(multiplexer_4_out));
  Add #(.Bits(32)) add_1 (.a(pc_1_dout), .b(32'h4), .c_i(1'b0), .s(add_1_s));  // open: c_o
  memory memory_1 (
    .address(alu_1_out), .din(regfile_1_r2), .op(controller_1_memory_op), .clk(clk), .rst(rst),
    .dout(memory_1_dout));
  Terminal terminal_1 (.D(regfile_1_r2), .C(clk), .en(controller_1_memory_op[3]));

  // Notes on the sheet:
  //   clk: Hz: 10
endmodule
